// Logisim project contador anel.circ as structural Verilog: 4 circuits, main circuit main
module main (
  input  CLEAR,
  input  ENABLE_CONTADOR
);

  wire clock_1_out, contador_1_saida, contador_anel_1_ligado, contador_anel_1_saida, ENABLE_out;
  wire [3:0] contador_1_saida_display, contador_2_saida_display;

  Clock clock_1 (.out(clock_1_out));
  Button ENABLE (.out(ENABLE_out));
  CONTADOR_ANEL contador_anel_1 (
    .CLOCK(clock_1_out), .ENTRADA(ENABLE_out), .CLEAR(CLEAR), .LIGADO(contador_anel_1_ligado),
    .SAIDA(contador_anel_1_saida));
  LED primerio_bit (.in(contador_anel_1_ligado));
  contador contador_1 (
    .CLOCK(contador_anel_1_saida), .Enable(ENABLE_CONTADOR), .SAIDA_DISPLAY(contador_1_saida_display),
    .SAIDA(contador_1_saida));
  Hex_Digit_Display hex_digit_display_1 (.value(contador_1_saida_display));  // open: dp
  Hex_Digit_Display hex_digit_display_2 (.value(contador_2_saida_display));  // open: dp
  contador contador_2 (
    .CLOCK(contador_1_saida), .Enable(ENABLE_CONTADOR), .SAIDA_DISPLAY(contador_2_saida_display));  // open: SAIDA
endmodule

module contador (
  input  Enable,
  input  CLOCK,
  output [3:0] SAIDA_DISPLAY,
  output SAIDA
);

  wire not_1_out, not_2_out, not_3_out, not_4_out;

  not not_1 (not_1_out, SAIDA_DISPLAY[2]);
  J_K_Flip_Flop j_k_ff_1 (
    .J(Enable), .clk(not_1_out), .K(Enable), .Q(SAIDA_DISPLAY[3]), .en(not_4_out), .reset(SAIDA));  // open: Qn, preset
  not not_2 (not_2_out, SAIDA_DISPLAY[1]);
  J_K_Flip_Flop j_k_ff_2 (
    .J(Enable), .clk(not_2_out), .K(Enable), .Q(SAIDA_DISPLAY[2]), .en(not_4_out), .reset(SAIDA));  // open: Qn, preset
  not not_3 (not_3_out, SAIDA_DISPLAY[0]);
  J_K_Flip_Flop j_k_ff_3 (
    .J(Enable), .clk(not_3_out), .K(Enable), .Q(SAIDA_DISPLAY[1]), .en(not_4_out), .reset(SAIDA));  // open: Qn, preset
  J_K_Flip_Flop j_k_ff_4 (
    .J(Enable), .clk(CLOCK), .K(Enable), .Q(SAIDA_DISPLAY[0]), .en(not_4_out), .reset(SAIDA));  // open: Qn, preset
  not not_4 (not_4_out, SAIDA);
  and and_1 (SAIDA, SAIDA_DISPLAY[3], SAIDA_DISPLAY[1]);
endmodule

module CONTADOR_ANEL (
  input  CLOCK,
  input  ENTRADA,
  input  CLEAR,
  output SAIDA,
  output LIGADO
);

  wire d_ff_2_q, d_ff_3_q, not_1_out, or_1_out;

  or or_1 (or_1_out, ENTRADA, SAIDA);
  not not_1 (not_1_out, CLEAR);
  D_Flip_Flop d_ff_1 (.clk(CLOCK), .D(or_1_out), .Q(LIGADO), .en(not_1_out), .reset(CLEAR));  // open: Qn, preset
  D_Flip_Flop d_ff_2 (.clk(CLOCK), .D(LIGADO), .Q(d_ff_2_q), .en(not_1_out), .reset(CLEAR));  // open: Qn, preset
  D_Flip_Flop d_ff_3 (.clk(CLOCK), .D(d_ff_2_q), .Q(d_ff_3_q), .en(not_1_out), .reset(CLEAR));  // open: Qn, preset
  D_Flip_Flop d_ff_4 (.clk(CLOCK), .D(d_ff_3_q), .Q(SAIDA), .en(not_1_out), .reset(CLEAR));  // open: Qn, preset
endmodule

module contador_de_anel_final (
  input  CLEAR,
  output SAIDA,
  output LIGADO
);

  wire clock_1_out, d_ff_2_q, d_ff_3_q, ENTRADA_out, not_1_out, or_1_out;

  Clock clock_1 (.out(clock_1_out));
  Button ENTRADA (.out(ENTRADA_out));
  or or_1 (or_1_out, ENTRADA_out, SAIDA);
  not not_1 (not_1_out, CLEAR);
  D_Flip_Flop d_ff_1 (.clk(clock_1_out), .D(or_1_out), .Q(LIGADO), .en(not_1_out), .reset(CLEAR));  // open: Qn, preset
  D_Flip_Flop d_ff_2 (.clk(clock_1_out), .D(LIGADO), .Q(d_ff_2_q), .en(not_1_out), .reset(CLEAR));  // open: Qn, preset
  D_Flip_Flop d_ff_3 (
    .clk(clock_1_out), .D(d_ff_2_q), .Q(d_ff_3_q), .en(not_1_out), .reset(CLEAR));  // open: Qn, preset
  D_Flip_Flop d_ff_4 (.clk(clock_1_out), .D(d_ff_3_q), .Q(SAIDA), .en(not_1_out), .reset(CLEAR));  // open: Qn, preset
endmodule
