// Logisim project contador_dec.circ as structural Verilog: 1 circuit, main circuit main
module main (
  input  Enable,
  input  Enable_2
);

  wire and_1_out, and_2_out, clock_1_out, clock_2_out, j_k_ff_2_q, j_k_ff_4_q, j_k_ff_6_q, j_k_ff_8_q,
       not_1_out, not_2_out, not_3_out, not_4_out, not_5_out, not_6_out, not_7_out, not_8_out;
  wire [3:0] j_k_ff_7_q;

  not not_1 (not_1_out, j_k_ff_7_q[2]);
  J_K_Flip_Flop j_k_ff_1 (
    .J(Enable), .clk(not_1_out), .K(Enable), .Q(j_k_ff_7_q[3]), .en(not_7_out), .reset(and_1_out));  // open: Qn, preset
  J_K_Flip_Flop j_k_ff_2 (
    .J(Enable_2), .clk(not_2_out), .K(Enable_2), .Q(j_k_ff_2_q), .en(not_8_out), .reset(and_2_out));  // open: Qn, preset
  not not_2 (not_2_out, j_k_ff_4_q);
  not not_3 (not_3_out, j_k_ff_7_q[1]);
  not not_4 (not_4_out, j_k_ff_6_q);
  J_K_Flip_Flop j_k_ff_3 (
    .J(Enable), .clk(not_3_out), .K(Enable), .Q(j_k_ff_7_q[2]), .en(not_7_out), .reset(and_1_out));  // open: Qn, preset
  not not_5 (not_5_out, j_k_ff_7_q[0]);
  J_K_Flip_Flop j_k_ff_4 (
    .J(Enable_2), .clk(not_4_out), .K(Enable_2), .Q(j_k_ff_4_q), .en(not_8_out), .reset(and_2_out));  // open: Qn, preset
  not not_6 (not_6_out, j_k_ff_8_q);
  Hex_Digit_Display hex_digit_display_1 (.value(j_k_ff_7_q));  // open: dp
  J_K_Flip_Flop j_k_ff_5 (
    .J(Enable), .clk(not_5_out), .K(Enable), .Q(j_k_ff_7_q[1]), .en(not_7_out), .reset(and_1_out));  // open: Qn, preset
  Clock clock_1 (.out(clock_1_out));
  J_K_Flip_Flop j_k_ff_6 (
    .J(Enable_2), .clk(not_6_out), .K(Enable_2), .Q(j_k_ff_6_q), .en(not_8_out), .reset(and_2_out));  // open: Qn, preset
  Clock clock_2 (.out(clock_2_out));
  J_K_Flip_Flop j_k_ff_7 (
    .J(Enable), .clk(clock_1_out), .K(Enable), .Q(j_k_ff_7_q[0]), .en(not_7_out), .reset(and_1_out));  // open: Qn, preset
  not not_7 (not_7_out, and_1_out);
  J_K_Flip_Flop j_k_ff_8 (
    .J(Enable_2), .clk(clock_2_out), .K(Enable_2), .Q(j_k_ff_8_q), .en(not_8_out), .reset(and_2_out));  // open: Qn, preset
  not not_8 (not_8_out, and_2_out);
  and and_1 (and_1_out, j_k_ff_7_q[3], j_k_ff_7_q[1]);
  and and_2 (and_2_out, j_k_ff_2_q, j_k_ff_6_q);
endmodule
