// Logisim project circuito RS com clock.circ as structural Verilog: 1 circuit, main circuit main
module main (
  input  Entrada_S,
  input  Entrada_R,
  output Saida_Q,
  output Saida_Q1
);

  wire clock_1_out, nand_1_out, nand_2_out;

  Clock clock_1 (.out(clock_1_out));
  nand nand_1 (nand_1_out, Entrada_S, clock_1_out);
  nand nand_2 (nand_2_out, clock_1_out, Entrada_R);
  nand nand_3 (Saida_Q, nand_1_out, Saida_Q1);
  nand nand_4 (Saida_Q1, Saida_Q, nand_2_out);
endmodule
